// Logisim project circuito_atual copy.circ as structural Verilog: 11 circuits, main circuit main
module main (
);

  soma_1_bit soma_1_bit_1 ();  // open: SOMA, VAI_1, A, B, VEM_1
endmodule

module mux_8_bits_8canais (
  input  Canal_0,
  input  Canal_1,
  input  Canal_2,
  input  Canal_3,
  input  Canal_4,
  input  Canal_5,
  input  Canal_6,
  input  Canal_7,
  input  Sel_2,
  input  Sel_1,
  input  Sel_0,
  output S
);

  wire and_1_out, and_2_out, and_3_out, and_4_out, and_5_out, and_6_out, and_7_out, and_8_out;

  and and_1 (and_1_out, Canal_0, ~Sel_2, ~Sel_1, ~Sel_0);  // AND_Gate
  and and_2 (and_2_out, Canal_1, ~Sel_2, ~Sel_1, Sel_0);  // AND_Gate
  and and_3 (and_3_out, Canal_2, ~Sel_2, Sel_1, ~Sel_0);  // AND_Gate
  and and_4 (and_4_out, Canal_3, ~Sel_2, Sel_1, Sel_0);  // AND_Gate
  and and_5 (and_5_out, Canal_4, Sel_2, ~Sel_1, ~Sel_0);  // AND_Gate
  and and_6 (and_6_out, Canal_5, Sel_2, ~Sel_1, Sel_0);  // AND_Gate
  and and_7 (and_7_out, Canal_6, Sel_2, Sel_1, ~Sel_0);  // AND_Gate
  and and_8 (and_8_out, Canal_7, Sel_2, Sel_1, Sel_0);
  or or_1 (S, and_1_out, and_2_out, and_3_out, and_4_out, and_5_out, and_6_out, and_7_out, and_8_out);
endmodule

module mux2 (
  input  Canal_0,
  input  Canal_1,
  input  Sel_0,
  output out_4
);

  wire and_1_out, and_2_out;

  and and_1 (and_1_out, ~Sel_0, Canal_0);  // AND_Gate
  and and_2 (and_2_out, Sel_0, Canal_1);
  or or_1 (out_4, and_1_out, and_2_out);
endmodule

module mux_16 (
  input  Canal_0,
  input  Canal_1,
  input  Canal_2,
  input  Canal_3,
  input  Canal_4,
  input  Canal_5,
  input  Canal_6,
  input  Canal_7,
  input  Canal_8,
  input  Canal_9,
  input  Canal_10,
  input  Canal_11,
  input  Canal_12,
  input  Canal_13,
  input  Canal_14,
  input  Canal_15,
  input  in_17,
  input  in_18,
  input  in_19,
  input  in_20,
  output out_21
);

  wire mux_8_bits_8canais_1_s, mux_8_bits_8canais_2_s;

  mux_8_bits_8canais mux_8_bits_8canais_1 (
    .Canal_0(Canal_0), .Canal_1(Canal_1), .Canal_2(Canal_2), .Canal_3(Canal_3), .Canal_4(Canal_4),
    .Canal_5(Canal_5), .Canal_6(Canal_6), .Canal_7(Canal_7), .Sel_2(in_18), .Sel_1(in_19), .Sel_0(in_20),
    .S(mux_8_bits_8canais_1_s));
  mux_8_bits_8canais mux_8_bits_8canais_2 (
    .Canal_0(Canal_8), .Canal_1(Canal_9), .Canal_2(Canal_10), .Canal_3(Canal_11), .Canal_4(Canal_12),
    .Canal_5(Canal_13), .Canal_6(Canal_14), .Canal_7(Canal_15), .Sel_2(in_18), .Sel_1(in_19), .Sel_0(in_20),
    .S(mux_8_bits_8canais_2_s));
  mux2 mux2_1 (.Canal_0(mux_8_bits_8canais_1_s), .Canal_1(mux_8_bits_8canais_2_s), .Sel_0(in_17), .out_4(out_21));
endmodule

module ula_1_bit (
  input  A,
  input  B,
  input  M,
  input  C_in,
  input  [2:0] Op_Sel,
  output Resultado,
  output C_out
);

  // XOR_Gate xor_1: pin names not known; wires that end beside it: B
  Somador_Completo somador_completo_1 (.Soma(C_out));  // open: out_5, A, B, in_3
  xor xor_2 (B, B, B);
  \mux_de_8_nova_versão  \mux_de_8_nova_versão_1  ();  // open: Canal_0, Canal_1, Canal_2, Canal_3, Canal_4, Canal_5, Canal_6, Canal_7, Saída, Seletor_2, Seletor_1, Seletor_0

  assign M = B;
endmodule

module soma_1_bit (
  input  A,
  input  B,
  input  VEM_1,
  output SOMA,
  output VAI_1
);

  wire and_1_out, and_2_out, and_3_out, xor_1_out;

  xor xor_1 (xor_1_out, B, A);
  and and_1 (and_1_out, A, VEM_1);
  and and_2 (and_2_out, A, B);
  and and_3 (and_3_out, B, VEM_1);
  xor xor_2 (SOMA, xor_1_out, VEM_1);
  or or_1 (VAI_1, and_1_out, and_2_out, and_3_out);
  mux_16 mux_16_1 ();  // open: Canal_0, Canal_1, Canal_2, Canal_3, Canal_4, Canal_5, Canal_6, Canal_7, Canal_8, Canal_9, Canal_10, Canal_11, Canal_12, Canal_13, Canal_14, Canal_15, in_17, in_18, in_19, in_20, out_21
endmodule

module \mux_de_8_nova_versão  (
  input  Canal_0,
  input  Canal_1,
  input  Canal_2,
  input  Canal_3,
  input  Canal_4,
  input  Canal_5,
  input  Canal_6,
  input  Canal_7,
  input  Seletor_2,
  input  Seletor_1,
  input  Seletor_0,
  output \Saída 
);

  wire mux2_1_out_4, mux2_3_out_4, mux2_4_out_4, mux2_5_out_4, mux2_6_out_4;

  mux2 mux2_1 (.Canal_0(Canal_0), .Canal_1(Canal_1), .Sel_0(Seletor_0), .out_4(mux2_1_out_4));
  mux2 mux2_2 (.Canal_0(Canal_2), .Canal_1(Canal_3), .Sel_0(Seletor_0), .out_4(Seletor_0));
  mux2 mux2_3 (.Canal_0(Canal_4), .Canal_1(Canal_5), .Sel_0(Seletor_0), .out_4(mux2_3_out_4));
  mux2 mux2_4 (.Canal_0(Canal_6), .Canal_1(Canal_7), .Sel_0(Seletor_0), .out_4(mux2_4_out_4));
  mux2 mux2_5 (.Canal_0(mux2_1_out_4), .Canal_1(Seletor_0), .Sel_0(Seletor_1), .out_4(mux2_5_out_4));
  mux2 mux2_6 (.Canal_0(mux2_3_out_4), .Canal_1(mux2_4_out_4), .Sel_0(Seletor_1), .out_4(mux2_6_out_4));
  mux2 mux2_7 (.Canal_0(mux2_5_out_4), .Canal_1(mux2_6_out_4), .Sel_0(Seletor_2), .out_4(\Saída ));
endmodule

module Somador_Completo (
  input  A,
  input  B,
  input  in_3,
  output Soma,
  output out_5
);

  wire and_1_out, and_2_out, and_3_out, xor_1_out;

  or or_1 (out_5, and_1_out, and_2_out, and_3_out);
  and and_1 (and_1_out, A, B);
  and and_2 (and_2_out, in_3, B);
  and and_3 (and_3_out, in_3, A);
  xor xor_1 (xor_1_out, A, B);
  xor xor_2 (Soma, in_3, xor_1_out);

  // Notes on the sheet:
  //   S = (A Xor B) Xor Te
  //   Ts = (B*te) + (A + B) + (A*Te)
endmodule

module ULA_32_Bits (
  input  [31:0] A,
  input  [31:0] B,
  input  [3:0] in_3,
  output [31:0] \Saída 
);

  wire ula_1_bit_1_c_out, ula_1_bit_2_c_out, ula_1_bit_3_c_out, ula_1_bit_4_c_out, ula_1_bit_5_c_out,
       ula_1_bit_6_c_out, ula_1_bit_7_c_out, ula_1_bit_8_c_out, ula_1_bit_9_c_out, ula_1_bit_10_c_out,
       ula_1_bit_11_c_out, ula_1_bit_12_c_out, ula_1_bit_13_c_out, ula_1_bit_14_c_out, ula_1_bit_15_c_out,
       ula_1_bit_16_c_out, ula_1_bit_17_c_out, ula_1_bit_18_c_out, ula_1_bit_19_c_out, ula_1_bit_20_c_out,
       ula_1_bit_21_c_out, ula_1_bit_22_c_out, ula_1_bit_23_c_out, ula_1_bit_24_c_out, ula_1_bit_25_c_out,
       ula_1_bit_26_c_out, ula_1_bit_27_c_out, ula_1_bit_28_c_out, ula_1_bit_29_c_out, ula_1_bit_30_c_out,
       ula_1_bit_31_c_out;

  ula_1_bit ula_1_bit_1 (
    .C_out({ula_1_bit_1_c_out, 1'bz}), .C_in(1'b0), .A(A[0]), .B(B[0]), .Op_Sel(in_3[2:0]),
    .Resultado(\Saída [0]));
  ula_1_bit ula_1_bit_2 (
    .C_out({ula_1_bit_2_c_out, 1'bz}), .C_in(ula_1_bit_31_c_out), .A(A[16]), .B(B[16]), .Op_Sel(in_3[2:0]),
    .Resultado(\Saída [16]));
  ula_1_bit ula_1_bit_3 (
    .C_out({ula_1_bit_3_c_out, 1'bz}), .C_in(ula_1_bit_1_c_out), .A(A[1]), .B(B[1]), .Op_Sel(in_3[2:0]),
    .Resultado(\Saída [1]));
  ula_1_bit ula_1_bit_4 (
    .C_out({ula_1_bit_4_c_out, 1'bz}), .C_in(ula_1_bit_2_c_out), .A(A[17]), .B(B[17]), .Op_Sel(in_3[2:0]),
    .Resultado(\Saída [17]));
  ula_1_bit ula_1_bit_5 (
    .C_out({ula_1_bit_5_c_out, 1'bz}), .C_in(ula_1_bit_3_c_out), .A(A[2]), .B(B[2]), .Op_Sel(in_3[2:0]),
    .Resultado(\Saída [2]));
  ula_1_bit ula_1_bit_6 (
    .C_out({ula_1_bit_6_c_out, 1'bz}), .C_in(ula_1_bit_4_c_out), .A(A[18]), .B(B[18]), .Op_Sel(in_3[2:0]),
    .Resultado(\Saída [18]));
  ula_1_bit ula_1_bit_7 (
    .C_out({ula_1_bit_7_c_out, 1'bz}), .C_in(ula_1_bit_5_c_out), .A(A[3]), .B(B[3]), .Op_Sel(in_3[2:0]),
    .Resultado(\Saída [3]));
  ula_1_bit ula_1_bit_8 (
    .C_out({ula_1_bit_8_c_out, 1'bz}), .C_in(ula_1_bit_6_c_out), .A(A[19]), .B(B[19]), .Op_Sel(in_3[2:0]),
    .Resultado(\Saída [19]));
  ula_1_bit ula_1_bit_9 (
    .C_out({ula_1_bit_9_c_out, 1'bz}), .C_in(ula_1_bit_7_c_out), .A(A[4]), .B(B[4]), .Op_Sel(in_3[2:0]),
    .Resultado(\Saída [4]));
  ula_1_bit ula_1_bit_10 (
    .C_out({ula_1_bit_10_c_out, 1'bz}), .C_in(ula_1_bit_8_c_out), .A(A[20]), .B(B[20]), .Op_Sel(in_3[2:0]),
    .Resultado(\Saída [20]));
  ula_1_bit ula_1_bit_11 (
    .C_out({ula_1_bit_11_c_out, 1'bz}), .C_in(ula_1_bit_9_c_out), .A(A[5]), .B(B[5]), .Op_Sel(in_3[2:0]),
    .Resultado(\Saída [5]));
  ula_1_bit ula_1_bit_12 (
    .C_out({ula_1_bit_12_c_out, 1'bz}), .C_in(ula_1_bit_10_c_out), .A(A[21]), .B(B[21]), .Op_Sel(in_3[2:0]),
    .Resultado(\Saída [21]));
  ula_1_bit ula_1_bit_13 (
    .C_out({ula_1_bit_13_c_out, 1'bz}), .C_in(ula_1_bit_11_c_out), .A(A[6]), .B(B[6]), .Op_Sel(in_3[2:0]),
    .Resultado(\Saída [6]));
  ula_1_bit ula_1_bit_14 (
    .C_out({ula_1_bit_14_c_out, 1'bz}), .C_in(ula_1_bit_12_c_out), .A(A[22]), .B(B[22]), .Op_Sel(in_3[2:0]),
    .Resultado(\Saída [22]));
  ula_1_bit ula_1_bit_15 (
    .C_out({ula_1_bit_15_c_out, 1'bz}), .C_in(ula_1_bit_13_c_out), .A(A[7]), .B(B[7]), .Op_Sel(in_3[2:0]),
    .Resultado(\Saída [7]));
  ula_1_bit ula_1_bit_16 (
    .C_out({ula_1_bit_16_c_out, 1'bz}), .C_in(ula_1_bit_14_c_out), .A(A[23]), .B(B[23]), .Op_Sel(in_3[2:0]),
    .Resultado(\Saída [23]));
  ula_1_bit ula_1_bit_17 (
    .C_out({ula_1_bit_17_c_out, 1'bz}), .C_in(ula_1_bit_15_c_out), .A(A[8]), .B(B[8]), .Op_Sel(in_3[2:0]),
    .Resultado(\Saída [8]));
  ula_1_bit ula_1_bit_18 (
    .C_out({ula_1_bit_18_c_out, 1'bz}), .C_in(ula_1_bit_16_c_out), .A(A[24]), .B(B[24]), .Op_Sel(in_3[2:0]),
    .Resultado(\Saída [24]));
  ula_1_bit ula_1_bit_19 (
    .C_out({ula_1_bit_19_c_out, 1'bz}), .C_in(ula_1_bit_17_c_out), .A(A[9]), .B(B[9]), .Op_Sel(in_3[2:0]),
    .Resultado(\Saída [9]));
  ula_1_bit ula_1_bit_20 (
    .C_out({ula_1_bit_20_c_out, 1'bz}), .C_in(ula_1_bit_18_c_out), .A(A[25]), .B(B[25]), .Op_Sel(in_3[2:0]),
    .Resultado(\Saída [25]));
  ula_1_bit ula_1_bit_21 (
    .C_out({ula_1_bit_21_c_out, 1'bz}), .C_in(ula_1_bit_19_c_out), .A(A[10]), .B(B[10]), .Op_Sel(in_3[2:0]),
    .Resultado(\Saída [10]));
  ula_1_bit ula_1_bit_22 (
    .C_out({ula_1_bit_22_c_out, 1'bz}), .C_in(ula_1_bit_20_c_out), .A(A[26]), .B(B[26]), .Op_Sel(in_3[2:0]),
    .Resultado(\Saída [26]));
  ula_1_bit ula_1_bit_23 (
    .C_out({ula_1_bit_23_c_out, 1'bz}), .C_in(ula_1_bit_21_c_out), .A(A[11]), .B(B[11]), .Op_Sel(in_3[2:0]),
    .Resultado(\Saída [11]));
  ula_1_bit ula_1_bit_24 (
    .C_out({ula_1_bit_24_c_out, 1'bz}), .C_in(ula_1_bit_22_c_out), .A(A[27]), .B(B[27]), .Op_Sel(in_3[2:0]),
    .Resultado(\Saída [27]));
  ula_1_bit ula_1_bit_25 (
    .C_out({ula_1_bit_25_c_out, 1'bz}), .C_in(ula_1_bit_23_c_out), .A(A[12]), .B(B[12]), .Op_Sel(in_3[2:0]),
    .Resultado(\Saída [12]));
  ula_1_bit ula_1_bit_26 (
    .C_out({ula_1_bit_26_c_out, 1'bz}), .C_in(ula_1_bit_24_c_out), .A(A[28]), .B(B[28]), .Op_Sel(in_3[2:0]),
    .Resultado(\Saída [28]));
  ula_1_bit ula_1_bit_27 (
    .C_out({ula_1_bit_27_c_out, 1'bz}), .C_in(ula_1_bit_25_c_out), .A(A[13]), .B(B[13]), .Op_Sel(in_3[2:0]),
    .Resultado(\Saída [13]));
  ula_1_bit ula_1_bit_28 (
    .C_out({ula_1_bit_28_c_out, 1'bz}), .C_in(ula_1_bit_26_c_out), .A(A[29]), .B(B[29]), .Op_Sel(in_3[2:0]),
    .Resultado(\Saída [29]));
  ula_1_bit ula_1_bit_29 (
    .C_out({ula_1_bit_29_c_out, 1'bz}), .C_in(ula_1_bit_27_c_out), .A(A[14]), .B(B[14]), .Op_Sel(in_3[2:0]),
    .Resultado(\Saída [14]));
  ula_1_bit ula_1_bit_30 (
    .C_out({ula_1_bit_30_c_out, 1'bz}), .C_in(ula_1_bit_28_c_out), .A(A[30]), .B(B[30]), .Op_Sel(in_3[2:0]),
    .Resultado(\Saída [30]));
  ula_1_bit ula_1_bit_31 (
    .C_out({ula_1_bit_31_c_out, 1'bz}), .C_in(ula_1_bit_29_c_out), .A(A[15]), .B(B[15]), .Op_Sel(in_3[2:0]),
    .Resultado(\Saída [15]));
  ula_1_bit ula_1_bit_32 (
    .C_in(ula_1_bit_30_c_out), .A(A[31]), .B(B[31]), .Op_Sel(in_3[2:0]), .Resultado(\Saída [31]));  // open: C_out
  // Pins of 3 and 4 bits meet at in_3

  // Other names for the same wires on the sheet: S0 = \Saída [0]; S1 = \Saída [1]; S2 = \Saída [2]; S3 = \Saída [3];
  //   S4 = \Saída [4]; S5 = \Saída [5]; S6 = \Saída [6]; S7 = \Saída [7]; S8 = \Saída [8]; S9 = \Saída [9];
  //   S10 = \Saída [10]; S11 = \Saída [11]; S12 = \Saída [12]; S13 = \Saída [13]; S14 = \Saída [14];
  //   S15 = \Saída [15]; S16 = \Saída [16]; S17 = \Saída [17]; S18 = \Saída [18]; S19 = \Saída [19];
  //   S20 = \Saída [20]; S21 = \Saída [21]; S22 = \Saída [22]; S23 = \Saída [23]; S24 = \Saída [24];
  //   S25 = \Saída [25]; S26 = \Saída [26]; S27 = \Saída [27]; S28 = \Saída [28]; S29 = \Saída [29];
  //   S30 = \Saída [30]; S31 = \Saída [31]
endmodule

module Sleft_de_bit (
  input  [31:0] in_1,
  input  [31:0] in_2,
  input  in_3
);

  Multiplexer #(.width(32)) multiplexer_1 (.in0(in_1), .in1({in_1[30:0], 1'b0}), .out(in_2), .sel(in_3));  // open: en
endmodule

module ula_de_1_bit_sem_porta_nand (
  input  A,
  input  B,
  input  Transporte_de_entrada,
  input  [3:0] Seletor,
  output Resultado,
  output \Transporte_de_saída 
);

  wire and_1_out, or_1_out, somador_completo_1_soma, xor_1_out;

  Somador_Completo somador_completo_1 (
    .out_5(\Transporte_de_saída ), .A(A), .B(B), .in_3(Transporte_de_entrada), .Soma(somador_completo_1_soma));
  and and_1 (and_1_out, A, B);
  or or_1 (or_1_out, A, B);
  xor xor_1 (xor_1_out, A, B);
  mux_16 mux_16_1 (
    .Canal_0(and_1_out), .Canal_1(or_1_out), .Canal_2(xor_1_out), .Canal_3(somador_completo_1_soma),
    .in_17(Seletor[3]), .in_18(Seletor[2]), .in_19(Seletor[1]), .in_20(Seletor[0]), .out_21(Resultado));  // open: Canal_4, Canal_5, Canal_6, Canal_7, Canal_8, Canal_9, Canal_10, Canal_11, Canal_12, Canal_13, Canal_14, Canal_15

  // Notes on the sheet:
  //   Trasnporte de entrada: Vai 1
  //   Transporte de saída: 
  //   Ula de 1 bit sem porta nand
  //   Tanto o te quando o ts são o mesmo vai 1, no entanto, o te está chegando, e o ts está saindo para a próxima operação no próximo bit
endmodule
