// Logisim project mux.circ as structural Verilog: 9 circuits, main circuit main
module main (
);

  soma_1_bit soma_1_bit_1 ();  // open: SOMA, VAI_1, A, B, VEM_1
endmodule

module mux_8_bits_8canais (
  input  Canal_0,
  input  Canal_1,
  input  Canal_2,
  input  Canal_3,
  input  Canal_4,
  input  Canal_5,
  input  Canal_6,
  input  Canal_7,
  input  Sel_2,
  input  Sel_1,
  input  Sel_0,
  output S
);

  wire and_1_out, and_2_out, and_3_out, and_4_out, and_5_out, and_6_out, and_7_out, and_8_out;

  and and_1 (and_1_out, Canal_0, ~Sel_2, ~Sel_1, ~Sel_0);  // AND_Gate
  and and_2 (and_2_out, Canal_1, ~Sel_2, ~Sel_1, Sel_0);  // AND_Gate
  and and_3 (and_3_out, Canal_2, ~Sel_2, Sel_1, ~Sel_0);  // AND_Gate
  and and_4 (and_4_out, Canal_3, ~Sel_2, Sel_1, Sel_0);  // AND_Gate
  and and_5 (and_5_out, Canal_4, Sel_2, ~Sel_1, ~Sel_0);  // AND_Gate
  and and_6 (and_6_out, Canal_5, Sel_2, ~Sel_1, Sel_0);  // AND_Gate
  and and_7 (and_7_out, Canal_6, Sel_2, Sel_1, ~Sel_0);  // AND_Gate
  and and_8 (and_8_out, Canal_7, Sel_2, Sel_1, Sel_0);
  or or_1 (S, and_1_out, and_2_out, and_3_out, and_4_out, and_5_out, and_6_out, and_7_out, and_8_out);
endmodule

module mux2 (
  input  Canal_0,
  input  Canal_1,
  input  Sel_0,
  output out_4
);

  wire and_1_out, and_2_out;

  and and_1 (and_1_out, ~Sel_0, Canal_0);  // AND_Gate
  and and_2 (and_2_out, Sel_0, Canal_1);
  or or_1 (out_4, and_1_out, and_2_out);
endmodule

module mux_16 (
  input  Canal_0,
  input  Canal_1,
  input  Canal_2,
  input  Canal_3,
  input  Canal_4,
  input  Canal_5,
  input  Canal_6,
  input  Canal_7,
  input  Canal_8,
  input  Canal_9,
  input  Canal_10,
  input  Canal_11,
  input  Canal_12,
  input  Canal_13,
  input  Canal_14,
  input  Canal_15,
  input  in_17,
  input  in_18,
  input  in_19,
  input  in_20,
  output out_21
);

  wire mux_8_bits_8canais_1_s, mux_8_bits_8canais_2_s;

  mux_8_bits_8canais mux_8_bits_8canais_1 (
    .Canal_0(Canal_0), .Canal_1(Canal_1), .Canal_2(Canal_2), .Canal_3(Canal_3), .Canal_4(Canal_4),
    .Canal_5(Canal_5), .Canal_6(Canal_6), .Canal_7(Canal_7), .Sel_2(in_18), .Sel_1(in_19), .Sel_0(in_20),
    .S(mux_8_bits_8canais_1_s));
  mux_8_bits_8canais mux_8_bits_8canais_2 (
    .Canal_0(Canal_8), .Canal_1(Canal_9), .Canal_2(Canal_10), .Canal_3(Canal_11), .Canal_4(Canal_12),
    .Canal_5(Canal_13), .Canal_6(Canal_14), .Canal_7(Canal_15), .Sel_2(in_18), .Sel_1(in_19), .Sel_0(in_20),
    .S(mux_8_bits_8canais_2_s));
  mux2 mux2_1 (.Canal_0(mux_8_bits_8canais_1_s), .Canal_1(mux_8_bits_8canais_2_s), .Sel_0(in_17), .out_4(out_21));
endmodule

module ula_1_bit (
  input  A,
  input  B,
  input  Transporte_de_entrada,
  input  [3:0] Seletor,
  output Resultado,
  output \Transporte_de_saída 
);

  wire and_1_out, or_1_out, somador_completo_1_soma, xor_1_out;

  Somador_Completo somador_completo_1 (
    .out_5(\Transporte_de_saída ), .A(A), .B(B), .in_3(Transporte_de_entrada), .Soma(somador_completo_1_soma));
  and and_1 (and_1_out, A, B);
  or or_1 (or_1_out, A, B);
  xor xor_1 (xor_1_out, A, B);
  mux_16 mux_16_1 (
    .Canal_0(and_1_out), .Canal_1(or_1_out), .Canal_2(xor_1_out), .Canal_3(somador_completo_1_soma),
    .in_17(Seletor[3]), .in_18(Seletor[2]), .in_19(Seletor[1]), .in_20(Seletor[0]), .out_21(Resultado));  // open: Canal_4, Canal_5, Canal_6, Canal_7, Canal_8, Canal_9, Canal_10, Canal_11, Canal_12, Canal_13, Canal_14, Canal_15
endmodule

module soma_1_bit (
  input  A,
  input  B,
  input  VEM_1,
  output SOMA,
  output VAI_1
);

  wire and_1_out, and_2_out, and_3_out, xor_1_out;

  xor xor_1 (xor_1_out, B, A);
  and and_1 (and_1_out, A, VEM_1);
  and and_2 (and_2_out, A, B);
  and and_3 (and_3_out, B, VEM_1);
  xor xor_2 (SOMA, xor_1_out, VEM_1);
  or or_1 (VAI_1, and_1_out, and_2_out, and_3_out);
  mux_16 mux_16_1 ();  // open: Canal_0, Canal_1, Canal_2, Canal_3, Canal_4, Canal_5, Canal_6, Canal_7, Canal_8, Canal_9, Canal_10, Canal_11, Canal_12, Canal_13, Canal_14, Canal_15, in_17, in_18, in_19, in_20, out_21
endmodule

module \mux_de_8_nova_versão  (
  input  Canal_0,
  input  Canal_1,
  input  Canal_2,
  input  Canal_3,
  input  Canal_4,
  input  Canal_5,
  input  Canal_6,
  input  Canal_7,
  input  Seletor_2,
  input  Seletor_1,
  input  Seletor_0,
  output \Saída 
);

  wire mux2_1_out_4, mux2_3_out_4, mux2_4_out_4, mux2_5_out_4, mux2_6_out_4;

  mux2 mux2_1 (.Canal_0(Canal_0), .Canal_1(Canal_1), .Sel_0(Seletor_0), .out_4(mux2_1_out_4));
  mux2 mux2_2 (.Canal_0(Canal_2), .Canal_1(Canal_3), .Sel_0(Seletor_0), .out_4(Seletor_0));
  mux2 mux2_3 (.Canal_0(Canal_4), .Canal_1(Canal_5), .Sel_0(Seletor_0), .out_4(mux2_3_out_4));
  mux2 mux2_4 (.Canal_0(Canal_6), .Canal_1(Canal_7), .Sel_0(Seletor_0), .out_4(mux2_4_out_4));
  mux2 mux2_5 (.Canal_0(mux2_1_out_4), .Canal_1(Seletor_0), .Sel_0(Seletor_1), .out_4(mux2_5_out_4));
  mux2 mux2_6 (.Canal_0(mux2_3_out_4), .Canal_1(mux2_4_out_4), .Sel_0(Seletor_1), .out_4(mux2_6_out_4));
  mux2 mux2_7 (.Canal_0(mux2_5_out_4), .Canal_1(mux2_6_out_4), .Sel_0(Seletor_2), .out_4(\Saída ));
endmodule

module Somador_Completo (
  input  A,
  input  B,
  input  in_3,
  output Soma,
  output out_5
);

  wire and_1_out, and_2_out, and_3_out, xor_1_out;

  or or_1 (out_5, and_1_out, and_2_out, and_3_out);
  and and_1 (and_1_out, A, B);
  and and_2 (and_2_out, in_3, B);
  and and_3 (and_3_out, in_3, A);
  xor xor_1 (xor_1_out, A, B);
  xor xor_2 (Soma, in_3, xor_1_out);
endmodule

module ULA_32_Bits (
  input  [31:0] A,
  input  [31:0] B,
  input  [3:0] in_3,
  output [31:0] Resultado
);

  wire ula_1_bit_1_resultado, ula_1_bit_2_resultado, ula_1_bit_3_resultado, ula_1_bit_4_resultado,
       ula_1_bit_5_resultado, ula_1_bit_6_resultado, ula_1_bit_7_resultado, ula_1_bit_8_resultado,
       ula_1_bit_9_resultado, ula_1_bit_10_resultado, ula_1_bit_11_resultado, ula_1_bit_12_resultado,
       ula_1_bit_13_resultado, ula_1_bit_14_resultado, ula_1_bit_15_resultado, ula_1_bit_16_resultado,
       ula_1_bit_17_resultado, ula_1_bit_18_resultado, ula_1_bit_19_resultado, ula_1_bit_20_resultado,
       ula_1_bit_21_resultado, ula_1_bit_22_resultado, ula_1_bit_23_resultado, ula_1_bit_24_resultado,
       ula_1_bit_25_resultado, ula_1_bit_26_resultado, ula_1_bit_27_resultado, ula_1_bit_28_resultado,
       ula_1_bit_29_resultado, ula_1_bit_30_resultado, ula_1_bit_31_resultado;

  ula_1_bit ula_1_bit_1 (
    .\Transporte_de_saída (Resultado[0]), .Transporte_de_entrada(B[0]), .A(A[0]), .B(1'b0), .Seletor(in_3),
    .Resultado(ula_1_bit_1_resultado));
  ula_1_bit ula_1_bit_2 (
    .\Transporte_de_saída (Resultado[16]), .Transporte_de_entrada(B[16]), .A(A[16]),
    .B(ula_1_bit_31_resultado), .Seletor(in_3), .Resultado(ula_1_bit_2_resultado));
  ula_1_bit ula_1_bit_3 (
    .\Transporte_de_saída (Resultado[1]), .Transporte_de_entrada(B[1]), .A(A[1]), .B(ula_1_bit_1_resultado),
    .Seletor(in_3), .Resultado(ula_1_bit_3_resultado));
  ula_1_bit ula_1_bit_4 (
    .\Transporte_de_saída (Resultado[17]), .Transporte_de_entrada(B[17]), .A(A[17]),
    .B(ula_1_bit_2_resultado), .Seletor(in_3), .Resultado(ula_1_bit_4_resultado));
  ula_1_bit ula_1_bit_5 (
    .\Transporte_de_saída (Resultado[2]), .Transporte_de_entrada(B[2]), .A(A[2]), .B(ula_1_bit_3_resultado),
    .Seletor(in_3), .Resultado(ula_1_bit_5_resultado));
  ula_1_bit ula_1_bit_6 (
    .\Transporte_de_saída (Resultado[18]), .Transporte_de_entrada(B[18]), .A(A[18]),
    .B(ula_1_bit_4_resultado), .Seletor(in_3), .Resultado(ula_1_bit_6_resultado));
  ula_1_bit ula_1_bit_7 (
    .\Transporte_de_saída (Resultado[3]), .Transporte_de_entrada(B[3]), .A(A[3]), .B(ula_1_bit_5_resultado),
    .Seletor(in_3), .Resultado(ula_1_bit_7_resultado));
  ula_1_bit ula_1_bit_8 (
    .\Transporte_de_saída (Resultado[19]), .Transporte_de_entrada(B[19]), .A(A[19]),
    .B(ula_1_bit_6_resultado), .Seletor(in_3), .Resultado(ula_1_bit_8_resultado));
  ula_1_bit ula_1_bit_9 (
    .\Transporte_de_saída (Resultado[4]), .Transporte_de_entrada(B[4]), .A(A[4]), .B(ula_1_bit_7_resultado),
    .Seletor(in_3), .Resultado(ula_1_bit_9_resultado));
  ula_1_bit ula_1_bit_10 (
    .\Transporte_de_saída (Resultado[20]), .Transporte_de_entrada(B[20]), .A(A[20]),
    .B(ula_1_bit_8_resultado), .Seletor(in_3), .Resultado(ula_1_bit_10_resultado));
  ula_1_bit ula_1_bit_11 (
    .\Transporte_de_saída (Resultado[5]), .Transporte_de_entrada(B[5]), .A(A[5]), .B(ula_1_bit_9_resultado),
    .Seletor(in_3), .Resultado(ula_1_bit_11_resultado));
  ula_1_bit ula_1_bit_12 (
    .\Transporte_de_saída (Resultado[21]), .Transporte_de_entrada(B[21]), .A(A[21]),
    .B(ula_1_bit_10_resultado), .Seletor(in_3), .Resultado(ula_1_bit_12_resultado));
  ula_1_bit ula_1_bit_13 (
    .\Transporte_de_saída (Resultado[6]), .Transporte_de_entrada(B[6]), .A(A[6]), .B(ula_1_bit_11_resultado),
    .Seletor(in_3), .Resultado(ula_1_bit_13_resultado));
  ula_1_bit ula_1_bit_14 (
    .\Transporte_de_saída (Resultado[22]), .Transporte_de_entrada(B[22]), .A(A[22]),
    .B(ula_1_bit_12_resultado), .Seletor(in_3), .Resultado(ula_1_bit_14_resultado));
  ula_1_bit ula_1_bit_15 (
    .\Transporte_de_saída (Resultado[7]), .Transporte_de_entrada(B[7]), .A(A[7]), .B(ula_1_bit_13_resultado),
    .Seletor(in_3), .Resultado(ula_1_bit_15_resultado));
  ula_1_bit ula_1_bit_16 (
    .\Transporte_de_saída (Resultado[23]), .Transporte_de_entrada(B[23]), .A(A[23]),
    .B(ula_1_bit_14_resultado), .Seletor(in_3), .Resultado(ula_1_bit_16_resultado));
  ula_1_bit ula_1_bit_17 (
    .\Transporte_de_saída (Resultado[8]), .Transporte_de_entrada(B[8]), .A(A[8]), .B(ula_1_bit_15_resultado),
    .Seletor(in_3), .Resultado(ula_1_bit_17_resultado));
  ula_1_bit ula_1_bit_18 (
    .\Transporte_de_saída (Resultado[24]), .Transporte_de_entrada(B[24]), .A(A[24]),
    .B(ula_1_bit_16_resultado), .Seletor(in_3), .Resultado(ula_1_bit_18_resultado));
  ula_1_bit ula_1_bit_19 (
    .\Transporte_de_saída (Resultado[9]), .Transporte_de_entrada(B[9]), .A(A[9]), .B(ula_1_bit_17_resultado),
    .Seletor(in_3), .Resultado(ula_1_bit_19_resultado));
  ula_1_bit ula_1_bit_20 (
    .\Transporte_de_saída (Resultado[25]), .Transporte_de_entrada(B[25]), .A(A[25]),
    .B(ula_1_bit_18_resultado), .Seletor(in_3), .Resultado(ula_1_bit_20_resultado));
  ula_1_bit ula_1_bit_21 (
    .\Transporte_de_saída (Resultado[10]), .Transporte_de_entrada(B[10]), .A(A[10]),
    .B(ula_1_bit_19_resultado), .Seletor(in_3), .Resultado(ula_1_bit_21_resultado));
  ula_1_bit ula_1_bit_22 (
    .\Transporte_de_saída (Resultado[26]), .Transporte_de_entrada(B[26]), .A(A[26]),
    .B(ula_1_bit_20_resultado), .Seletor(in_3), .Resultado(ula_1_bit_22_resultado));
  ula_1_bit ula_1_bit_23 (
    .\Transporte_de_saída (Resultado[11]), .Transporte_de_entrada(B[11]), .A(A[11]),
    .B(ula_1_bit_21_resultado), .Seletor(in_3), .Resultado(ula_1_bit_23_resultado));
  ula_1_bit ula_1_bit_24 (
    .\Transporte_de_saída (Resultado[27]), .Transporte_de_entrada(B[27]), .A(A[27]),
    .B(ula_1_bit_22_resultado), .Seletor(in_3), .Resultado(ula_1_bit_24_resultado));
  ula_1_bit ula_1_bit_25 (
    .\Transporte_de_saída (Resultado[12]), .Transporte_de_entrada(B[12]), .A(A[12]),
    .B(ula_1_bit_23_resultado), .Seletor(in_3), .Resultado(ula_1_bit_25_resultado));
  ula_1_bit ula_1_bit_26 (
    .\Transporte_de_saída (Resultado[28]), .Transporte_de_entrada(B[28]), .A(A[28]),
    .B(ula_1_bit_24_resultado), .Seletor(in_3), .Resultado(ula_1_bit_26_resultado));
  ula_1_bit ula_1_bit_27 (
    .\Transporte_de_saída (Resultado[13]), .Transporte_de_entrada(B[13]), .A(A[13]),
    .B(ula_1_bit_25_resultado), .Seletor(in_3), .Resultado(ula_1_bit_27_resultado));
  ula_1_bit ula_1_bit_28 (
    .\Transporte_de_saída (Resultado[29]), .Transporte_de_entrada(B[29]), .A(A[29]),
    .B(ula_1_bit_26_resultado), .Seletor(in_3), .Resultado(ula_1_bit_28_resultado));
  ula_1_bit ula_1_bit_29 (
    .\Transporte_de_saída (Resultado[14]), .Transporte_de_entrada(B[14]), .A(A[14]),
    .B(ula_1_bit_27_resultado), .Seletor(in_3), .Resultado(ula_1_bit_29_resultado));
  ula_1_bit ula_1_bit_30 (
    .\Transporte_de_saída (Resultado[30]), .Transporte_de_entrada(B[30]), .A(A[30]),
    .B(ula_1_bit_28_resultado), .Seletor(in_3), .Resultado(ula_1_bit_30_resultado));
  ula_1_bit ula_1_bit_31 (
    .\Transporte_de_saída (Resultado[15]), .Transporte_de_entrada(B[15]), .A(A[15]),
    .B(ula_1_bit_29_resultado), .Seletor(in_3), .Resultado(ula_1_bit_31_resultado));
  // ula_1_bit ula_1_bit_32: pin names not known; wires that end beside it: ula_1_bit_30_resultado, A[31], in_3, B[31], Resultado[31]

  // Other names for the same wires on the sheet: S0 = Resultado[0]; S1 = Resultado[1]; S2 = Resultado[2];
  //   S3 = Resultado[3]; S4 = Resultado[4]; S5 = Resultado[5]; S6 = Resultado[6]; S7 = Resultado[7];
  //   S8 = Resultado[8]; S9 = Resultado[9]; S10 = Resultado[10]; S11 = Resultado[11]; S12 = Resultado[12];
  //   S13 = Resultado[13]; S14 = Resultado[14]; S15 = Resultado[15]; S16 = Resultado[16]; S17 = Resultado[17];
  //   S18 = Resultado[18]; S19 = Resultado[19]; S20 = Resultado[20]; S21 = Resultado[21]; S22 = Resultado[22];
  //   S23 = Resultado[23]; S24 = Resultado[24]; S25 = Resultado[25]; S26 = Resultado[26]; S27 = Resultado[27];
  //   S28 = Resultado[28]; S29 = Resultado[29]; S30 = Resultado[30]; S31 = Resultado[31]
endmodule
